// Logisim project Simulation.circ as structural Verilog: 1 circuit, main circuit main
module main (
);

  wire CLK, n74181_2_p1, n74181_2_p4, n74181_2_p24, RST;
  wire [3:0] n74181_2_p21;
  wire [6:0] n74181_2_p2;
  wire [7:0] A_q, B_q, BUS8, dipswitch_2_sw8, MAR_H_q, MAR_L_q;
  wire [11:0] n74181_1_p11;
  wire [14:0] dipswitch_1_sw13;
  wire [15:0] C_q, counter_2_q, MEMBUS16;
  wire [15:8] counter_1_q;

  assign MEMBUS16 = dipswitch_1_sw13[0] ? {counter_1_q, 8'h1} : 16'bz;  // Controlled_Buffer controlled_buffer_1
  assign MEMBUS16[15:8] = BUS8;  // Buffer buffer_1, 8 bits wide
  assign MEMBUS16[7:0] = BUS8;  // Buffer buffer_2, 8 bits wide
  assign MEMBUS16 = dipswitch_1_sw13[7] ? C_q : 16'bz;  // Controlled_Buffer controlled_buffer_2
  assign MEMBUS16 = dipswitch_1_sw13[10] ? {MAR_H_q, MAR_L_q} : 16'bz;  // Controlled_Buffer controlled_buffer_3
  assign BUS8 = n74181_1_p11[7] ? B_q : 8'bz;  // Controlled_Buffer controlled_buffer_4
  assign BUS8 = n74181_1_p11[9] ? A_q : 8'bz;  // Controlled_Buffer controlled_buffer_5
  assign BUS8 = n74181_1_p11[11] ? {n74181_2_p21[2], n74181_2_p2} : 8'bz;  // Controlled_Buffer controlled_buffer_6
  Counter counter_1 (
    .load(dipswitch_1_sw13[1]), .D(BUS8), .count(dipswitch_1_sw13[2]), .Q(counter_1_q), .up(1'b0), .clk(CLK),
    .clr(RST));  // open: carry
  Register D (.D(MEMBUS16[15:8]), .en(dipswitch_1_sw13[6]), .clk(CLK), .Q(C_q[15:8]), .clr(RST));
  Register C (.D(MEMBUS16[7:0]), .en(dipswitch_1_sw13[4]), .clk(CLK), .Q(C_q[7:0]), .clr(RST));
  Register MAR_H (.D(MEMBUS16[15:8]), .en(dipswitch_1_sw13[11]), .clk(CLK), .Q(MAR_H_q), .clr(RST));
  Register MAR_L (.D(MEMBUS16[7:0]), .en(dipswitch_1_sw13[11]), .clk(CLK), .Q(MAR_L_q), .clr(RST));
  Counter #(.max('hffff), .width(16)) counter_2 (
    .load(dipswitch_1_sw13[9]), .D(MEMBUS16), .count(dipswitch_1_sw13[14]), .Q(counter_2_q), .up(1'b1),
    .clk(CLK), .clr(RST));  // open: carry
  Register B (.D(BUS8), .en(n74181_1_p11[8]), .clk(CLK), .Q(B_q), .clr(RST));
  Register A (.D(BUS8), .en(n74181_1_p11[10]), .clk(CLK), .Q(A_q), .clr(RST));
  assign BUS8 = dipswitch_1_sw13[5] ? C_q[15:8] : 8'bz;  // Controlled_Buffer controlled_buffer_7
  assign BUS8 = dipswitch_1_sw13[3] ? C_q[7:0] : 8'bz;  // Controlled_Buffer controlled_buffer_8
  assign MEMBUS16 = dipswitch_1_sw13[8] ? counter_2_q : 16'bz;  // Controlled_Buffer controlled_buffer_9
  // _74181 74181_1: pin names not known; wires that end beside it: B_q[0], A_q[1], A_q[0], B_q[1], n74181_1_p11[3], A_q[2], n74181_1_p11[2], B_q[2], n74181_1_p11[1], A_q[3], n74181_1_p11[0], B_q[3], n74181_1_p11[5], n74181_1_p11[4]
  RAM #(.addrWidth(16)) ram_1 (
    .addr({MAR_H_q, MAR_L_q}), .we(dipswitch_1_sw13[13]), .oe(dipswitch_1_sw13[12]), .clk(CLK), .din(BUS8));  // open: dout
  // _74181 74181_2: pin names not known; wires that end beside it: n74181_2_p1, n74181_2_p2[0], n74181_2_p2[1], n74181_2_p4, n74181_2_p2[2], n74181_2_p2[3], B_q[4], A_q[5], A_q[4], B_q[5], n74181_1_p11[3], A_q[6], n74181_1_p11[2], B_q[6], n74181_1_p11[1], A_q[7], n74181_1_p11[0], B_q[7], n74181_2_p1, n74181_1_p11[4], n74181_2_p21[0], n74181_2_p2[4], n74181_2_p2[5], n74181_2_p24, n74181_2_p2[6], n74181_2_p21[2]
  and and_1 (n74181_2_p21[3], n74181_2_p4, n74181_2_p24);
  Register #(.width(4)) F (.D(n74181_2_p21), .en(n74181_1_p11[6]), .clk(CLK), .clr(RST));  // open: Q
  Button button_1 (.out(RST));
  and and_2 (n74181_2_p21[1], ~n74181_2_p2[0], ~n74181_2_p2[1], ~n74181_2_p2[2], ~n74181_2_p2[3], ~n74181_2_p2[4], ~n74181_2_p2[5], ~n74181_2_p2[6], ~n74181_2_p21[2]);  // AND_Gate
  Button button_2 (.out(CLK));
  DipSwitch #(.number(27)) dipswitch_1 (
    .sw1(n74181_1_p11[0]), .sw2(n74181_1_p11[1]), .sw3(n74181_1_p11[2]), .sw4(n74181_1_p11[3]),
    .sw5(n74181_1_p11[4]), .sw6(n74181_1_p11[5]), .sw7(n74181_1_p11[6]), .sw8(n74181_1_p11[7]),
    .sw9(n74181_1_p11[8]), .sw10(n74181_1_p11[9]), .sw11(n74181_1_p11[10]), .sw12(n74181_1_p11[11]),
    .sw13(dipswitch_1_sw13[0]), .sw14(dipswitch_1_sw13[1]), .sw15(dipswitch_1_sw13[2]),
    .sw16(dipswitch_1_sw13[3]), .sw17(dipswitch_1_sw13[4]), .sw18(dipswitch_1_sw13[5]),
    .sw19(dipswitch_1_sw13[6]), .sw20(dipswitch_1_sw13[7]), .sw21(dipswitch_1_sw13[8]),
    .sw22(dipswitch_1_sw13[9]), .sw23(dipswitch_1_sw13[10]), .sw24(dipswitch_1_sw13[11]),
    .sw25(dipswitch_1_sw13[12]), .sw26(dipswitch_1_sw13[13]), .sw27(dipswitch_1_sw13[14]));
  DipSwitch dipswitch_2 (
    .sw1(dipswitch_2_sw8[7]), .sw2(dipswitch_2_sw8[6]), .sw3(dipswitch_2_sw8[5]), .sw4(dipswitch_2_sw8[4]),
    .sw5(dipswitch_2_sw8[3]), .sw6(dipswitch_2_sw8[2]), .sw7(dipswitch_2_sw8[1]), .sw8(dipswitch_2_sw8[0]));
endmodule
